// Logisim project LAB3.circ as structural Verilog: 10 circuits, main circuit onebitfulladder
module main (
  input  I30,
  input  I14,
  input  I13,
  input  I12,
  input  I6,
  input  I5,
  input  I4,
  output ALUCTRL3,
  output ALUCTRL2,
  output ALUCTRL1,
  output ALUCTRL0,
  output ALUSRC
);

  wire and_1_out, not_1_out, not_2_out, not_3_out, not_4_out, not_5_out;

  not not_1 (not_1_out, I14);
  not not_2 (not_2_out, I13);
  not not_3 (not_3_out, I12);
  not not_4 (not_4_out, I5);
  not not_5 (not_5_out, I4);
  or or_1 (ALUCTRL1, not_2_out, not_5_out);
  and and_1 (and_1_out, I13, not_3_out);
  or or_2 (ALUSRC, not_4_out, not_5_out);
  or or_3 (ALUCTRL0, not_1_out, and_1_out);

  assign ALUCTRL2 = 1'b0;
  assign ALUCTRL3 = 1'b0;
endmodule

module onebitfulladder (
  input  A,
  input  B,
  input  Cin,
  output Result,
  output Cout
);

  wire and_1_out, and_2_out, and_3_out, and_4_out, and_5_out, and_6_out, and_7_out, not_1_out, not_2_out,
       not_3_out;

  not not_1 (not_1_out, A);
  not not_2 (not_2_out, B);
  not not_3 (not_3_out, Cin);
  and and_1 (and_1_out, not_1_out, not_2_out, Cin);
  and and_2 (and_2_out, not_1_out, B, not_3_out);
  and and_3 (and_3_out, A, not_2_out, not_3_out);
  and and_4 (and_4_out, A, B, Cin);
  and and_5 (and_5_out, B, Cin);
  and and_6 (and_6_out, A, Cin);
  and and_7 (and_7_out, A, B);
  or or_1 (Result, and_1_out, and_2_out, and_3_out, and_4_out);
  or or_2 (Cout, and_5_out, and_6_out, and_7_out);
endmodule

module one_bit_alu (
  input  [3:0] ALU_CTRL,
  input  A,
  input  B,
  input  Cin,
  output R,
  output Cout
);

  wire and_1_out, multiplexer_1_out, not_1_out, onebitfulladder_1_result, or_1_out, xor_1_out;

  not not_1 (not_1_out, B);
  Multiplexer #(.enable("false")) multiplexer_1 (.in0(B), .in1(not_1_out), .out(multiplexer_1_out), .sel(ALU_CTRL[2]));
  and and_1 (and_1_out, A, multiplexer_1_out);
  or or_1 (or_1_out, A, multiplexer_1_out);
  xor xor_1 (xor_1_out, A, multiplexer_1_out);
  Multiplexer #(.enable("false"), .select(2)) multiplexer_2 (
    .in0(and_1_out), .in1(or_1_out), .in2(xor_1_out), .in3(onebitfulladder_1_result), .out(R),
    .sel(ALU_CTRL[1:0]));
  onebitfulladder onebitfulladder_1 (
    .A(A), .B(multiplexer_1_out), .Cin(Cin), .Result(onebitfulladder_1_result), .Cout(Cout));
endmodule

module fourbitalu (
  input  [3:0] ALU_Ctrl,
  input  [3:0] A,
  input  [3:0] B,
  input  Cin,
  output [3:0] R,
  output Cout
);

  wire one_bit_alu_1_cout, one_bit_alu_2_cout, one_bit_alu_3_cout;

  one_bit_alu one_bit_alu_1 (.ALU_CTRL(ALU_Ctrl), .A(A[0]), .B(B[0]), .Cin(Cin), .R(R[0]), .Cout(one_bit_alu_1_cout));
  one_bit_alu one_bit_alu_2 (
    .ALU_CTRL(ALU_Ctrl), .A(A[1]), .B(B[1]), .Cin(one_bit_alu_1_cout), .R(R[1]), .Cout(one_bit_alu_2_cout));
  one_bit_alu one_bit_alu_3 (
    .ALU_CTRL(ALU_Ctrl), .A(A[2]), .B(B[2]), .Cin(one_bit_alu_2_cout), .R(R[2]), .Cout(one_bit_alu_3_cout));
  one_bit_alu one_bit_alu_4 (.ALU_CTRL(ALU_Ctrl), .A(A[3]), .B(B[3]), .Cin(one_bit_alu_3_cout), .R(R[3]), .Cout(Cout));
endmodule

module ALU32 (
  input  [3:0] ALU_Ctrl,
  input  [31:0] A,
  input  [31:0] B,
  output [31:0] R,
  output Cout
);

  wire fourbitalu_1_cout, fourbitalu_2_cout, fourbitalu_3_cout, fourbitalu_4_cout, fourbitalu_5_cout,
       fourbitalu_6_cout, fourbitalu_7_cout;

  fourbitalu fourbitalu_1 (
    .ALU_Ctrl(ALU_Ctrl), .A(A[3:0]), .B(B[3:0]), .Cin(ALU_Ctrl[2]), .R(R[3:0]), .Cout(fourbitalu_1_cout));
  fourbitalu fourbitalu_2 (
    .ALU_Ctrl(ALU_Ctrl), .A(A[7:4]), .B(B[7:4]), .Cin(fourbitalu_1_cout), .R(R[7:4]), .Cout(fourbitalu_2_cout));
  fourbitalu fourbitalu_3 (
    .ALU_Ctrl(ALU_Ctrl), .A(A[11:8]), .B(B[11:8]), .Cin(fourbitalu_2_cout), .R(R[11:8]),
    .Cout(fourbitalu_3_cout));
  fourbitalu fourbitalu_4 (
    .ALU_Ctrl(ALU_Ctrl), .A(A[15:12]), .B(B[15:12]), .Cin(fourbitalu_3_cout), .R(R[15:12]),
    .Cout(fourbitalu_4_cout));
  fourbitalu fourbitalu_5 (
    .A(A[19:16]), .B(B[19:16]), .Cin(fourbitalu_4_cout), .R(R[19:16]), .Cout(fourbitalu_5_cout));  // open: ALU_Ctrl
  fourbitalu fourbitalu_6 (
    .ALU_Ctrl(ALU_Ctrl), .A(A[23:20]), .B(B[23:20]), .Cin(fourbitalu_5_cout), .R(R[23:20]),
    .Cout(fourbitalu_6_cout));
  fourbitalu fourbitalu_7 (
    .ALU_Ctrl(ALU_Ctrl), .A(A[27:24]), .B(B[27:24]), .Cin(fourbitalu_6_cout), .R(R[27:24]),
    .Cout(fourbitalu_7_cout));
  fourbitalu fourbitalu_8 (
    .ALU_Ctrl(ALU_Ctrl), .A(A[31:28]), .B(B[31:28]), .Cin(fourbitalu_7_cout), .R(R[31:28]), .Cout(Cout));
endmodule

module RegisterFile (
  input  [4:0] RReg2,
  input  [4:0] RReg1,
  input  [31:0] WData,
  input  ClockIn,
  input  Write,
  input  [4:0] WReg,
  output [31:0] RData1,
  output [31:0] RData2
);

  wire demultiplexer_1_out0, demultiplexer_1_out1, demultiplexer_1_out2, demultiplexer_1_out3,
       demultiplexer_1_out4, demultiplexer_1_out5, demultiplexer_1_out6, demultiplexer_1_out7,
       demultiplexer_1_out8, demultiplexer_1_out9, demultiplexer_1_out10, demultiplexer_1_out11,
       demultiplexer_1_out12, demultiplexer_1_out13, demultiplexer_1_out14, demultiplexer_1_out15,
       demultiplexer_1_out16, demultiplexer_1_out17, demultiplexer_1_out18, demultiplexer_1_out19,
       demultiplexer_1_out20, demultiplexer_1_out21, demultiplexer_1_out22, demultiplexer_1_out23,
       demultiplexer_1_out24, demultiplexer_1_out25, demultiplexer_1_out26, demultiplexer_1_out27,
       demultiplexer_1_out28, demultiplexer_1_out29, demultiplexer_1_out30, demultiplexer_1_out31;
  wire [31:0] register_1_q, register_2_q, register_3_q, register_4_q, register_5_q, register_6_q,
       register_7_q, register_8_q, register_9_q, register_10_q, register_11_q, register_12_q, register_13_q,
       register_14_q, register_15_q, register_16_q, register_17_q, register_18_q, register_19_q,
       register_20_q, register_21_q, register_22_q, register_23_q, register_24_q, register_25_q,
       register_26_q, register_27_q, register_28_q, register_29_q, register_30_q, register_31_q,
       register_32_q;

  Demultiplexer #(.enable("false"), .select(5)) demultiplexer_1 (
    .out0(demultiplexer_1_out0), .out1(demultiplexer_1_out1), .out2(demultiplexer_1_out2),
    .out3(demultiplexer_1_out3), .out4(demultiplexer_1_out4), .out5(demultiplexer_1_out5),
    .out6(demultiplexer_1_out6), .out7(demultiplexer_1_out7), .out8(demultiplexer_1_out8),
    .out9(demultiplexer_1_out9), .out10(demultiplexer_1_out10), .out11(demultiplexer_1_out11),
    .out12(demultiplexer_1_out12), .out13(demultiplexer_1_out13), .out14(demultiplexer_1_out14),
    .out15(demultiplexer_1_out15), .out16(demultiplexer_1_out16), .out17(demultiplexer_1_out17),
    .out18(demultiplexer_1_out18), .out19(demultiplexer_1_out19), .out20(demultiplexer_1_out20),
    .out21(demultiplexer_1_out21), .out22(demultiplexer_1_out22), .out23(demultiplexer_1_out23),
    .out24(demultiplexer_1_out24), .out25(demultiplexer_1_out25), .out26(demultiplexer_1_out26),
    .out27(demultiplexer_1_out27), .out28(demultiplexer_1_out28), .out29(demultiplexer_1_out29),
    .out30(demultiplexer_1_out30), .out31(demultiplexer_1_out31), .in(Write), .sel(WReg));
  Register #(.width(32)) register_1 (
    .D(WData), .en(demultiplexer_1_out0), .clk(ClockIn), .Q(register_1_q), .clr(Write));
  Register #(.width(32)) register_2 (
    .D(WData), .en(demultiplexer_1_out1), .clk(ClockIn), .Q(register_2_q));  // open: clr
  Register #(.width(32)) register_3 (
    .D(WData), .en(demultiplexer_1_out2), .clk(ClockIn), .Q(register_3_q));  // open: clr
  Register #(.width(32)) register_4 (
    .D(WData), .en(demultiplexer_1_out3), .clk(ClockIn), .Q(register_4_q));  // open: clr
  Register #(.width(32)) register_5 (
    .D(WData), .en(demultiplexer_1_out4), .clk(ClockIn), .Q(register_5_q));  // open: clr
  Register #(.width(32)) register_6 (
    .D(WData), .en(demultiplexer_1_out5), .clk(ClockIn), .Q(register_6_q));  // open: clr
  Register #(.width(32)) register_7 (
    .D(WData), .en(demultiplexer_1_out6), .clk(ClockIn), .Q(register_7_q));  // open: clr
  Register #(.width(32)) register_8 (
    .D(WData), .en(demultiplexer_1_out7), .clk(ClockIn), .Q(register_8_q));  // open: clr
  Register #(.width(32)) register_9 (
    .D(WData), .en(demultiplexer_1_out8), .clk(ClockIn), .Q(register_9_q));  // open: clr
  Register #(.width(32)) register_10 (
    .D(WData), .en(demultiplexer_1_out9), .clk(ClockIn), .Q(register_10_q));  // open: clr
  Register #(.width(32)) register_11 (
    .D(WData), .en(demultiplexer_1_out10), .clk(ClockIn), .Q(register_11_q));  // open: clr
  Register #(.width(32)) register_12 (
    .D(WData), .en(demultiplexer_1_out11), .clk(ClockIn), .Q(register_12_q));  // open: clr
  Register #(.width(32)) register_13 (
    .D(WData), .en(demultiplexer_1_out12), .clk(ClockIn), .Q(register_13_q));  // open: clr
  Register #(.width(32)) register_14 (
    .D(WData), .en(demultiplexer_1_out13), .clk(ClockIn), .Q(register_14_q));  // open: clr
  Register #(.width(32)) register_15 (
    .D(WData), .en(demultiplexer_1_out14), .clk(ClockIn), .Q(register_15_q));  // open: clr
  Register #(.width(32)) register_16 (
    .D(WData), .en(demultiplexer_1_out15), .clk(ClockIn), .Q(register_16_q));  // open: clr
  Register #(.width(32)) register_17 (
    .D(WData), .en(demultiplexer_1_out16), .clk(ClockIn), .Q(register_17_q));  // open: clr
  Register #(.width(32)) register_18 (
    .D(WData), .en(demultiplexer_1_out17), .clk(ClockIn), .Q(register_18_q));  // open: clr
  Register #(.width(32)) register_19 (
    .D(WData), .en(demultiplexer_1_out18), .clk(ClockIn), .Q(register_19_q));  // open: clr
  Register #(.width(32)) register_20 (
    .D(WData), .en(demultiplexer_1_out19), .clk(ClockIn), .Q(register_20_q));  // open: clr
  Register #(.width(32)) register_21 (
    .D(WData), .en(demultiplexer_1_out20), .clk(ClockIn), .Q(register_21_q));  // open: clr
  Register #(.width(32)) register_22 (
    .D(WData), .en(demultiplexer_1_out21), .clk(ClockIn), .Q(register_22_q));  // open: clr
  Register #(.width(32)) register_23 (
    .D(WData), .en(demultiplexer_1_out22), .clk(ClockIn), .Q(register_23_q));  // open: clr
  Register #(.width(32)) register_24 (
    .D(WData), .en(demultiplexer_1_out23), .clk(ClockIn), .Q(register_24_q));  // open: clr
  Register #(.width(32)) register_25 (
    .D(WData), .en(demultiplexer_1_out24), .clk(ClockIn), .Q(register_25_q));  // open: clr
  Register #(.width(32)) register_26 (
    .D(WData), .en(demultiplexer_1_out25), .clk(ClockIn), .Q(register_26_q));  // open: clr
  Register #(.width(32)) register_27 (
    .D(WData), .en(demultiplexer_1_out26), .clk(ClockIn), .Q(register_27_q));  // open: clr
  Register #(.width(32)) register_28 (
    .D(WData), .en(demultiplexer_1_out27), .clk(ClockIn), .Q(register_28_q));  // open: clr
  Register #(.width(32)) register_29 (
    .D(WData), .en(demultiplexer_1_out28), .clk(ClockIn), .Q(register_29_q));  // open: clr
  Register #(.width(32)) register_30 (
    .D(WData), .en(demultiplexer_1_out29), .clk(ClockIn), .Q(register_30_q));  // open: clr
  Register #(.width(32)) register_31 (
    .D(WData), .en(demultiplexer_1_out30), .clk(ClockIn), .Q(register_31_q));  // open: clr
  Register #(.width(32)) register_32 (
    .D(WData), .en(demultiplexer_1_out31), .clk(ClockIn), .Q(register_32_q));  // open: clr
  Multiplexer #(.enable("false"), .select(5), .width(32)) multiplexer_1 (
    .in0(register_1_q), .in1(register_2_q), .in2(register_3_q), .in3(register_4_q), .in4(register_5_q),
    .in5(register_6_q), .in6(register_7_q), .in7(register_8_q), .in8(register_9_q), .in9(register_10_q),
    .in10(register_11_q), .in11(register_12_q), .in12(register_13_q), .in13(register_14_q),
    .in14(register_15_q), .in15(register_16_q), .in16(register_17_q), .in17(register_18_q),
    .in18(register_19_q), .in19(register_20_q), .in20(register_21_q), .in21(register_22_q),
    .in22(register_23_q), .in23(register_24_q), .in24(register_25_q), .in25(register_26_q),
    .in26(register_27_q), .in27(register_28_q), .in28(register_29_q), .in29(register_30_q),
    .in30(register_31_q), .in31(register_32_q), .out(RData1), .sel(RReg1));
  Multiplexer #(.enable("false"), .select(5), .width(32)) multiplexer_2 (
    .in0(register_1_q), .in1(register_2_q), .in2(register_3_q), .in3(register_4_q), .in4(register_5_q),
    .in5(register_6_q), .in6(register_7_q), .in7(register_8_q), .in8(register_9_q), .in9(register_10_q),
    .in10(register_11_q), .in11(register_12_q), .in12(register_13_q), .in13(register_14_q),
    .in14(register_15_q), .in15(register_16_q), .in16(register_17_q), .in17(register_18_q),
    .in18(register_19_q), .in19(register_20_q), .in20(register_21_q), .in21(register_22_q),
    .in22(register_23_q), .in23(register_24_q), .in24(register_25_q), .in25(register_26_q),
    .in26(register_27_q), .in27(register_28_q), .in28(register_29_q), .in29(register_30_q),
    .in30(register_31_q), .in31(register_32_q), .out(RData2), .sel(RReg2));
endmodule

module ALUControl (
  input  I30,
  input  I14,
  input  I13,
  input  I12,
  input  I6,
  input  I5,
  input  I4,
  output ALUCTRL3,
  output ALUCTRL2,
  output ALUCTRL1,
  output ALUCTRL0,
  output ALUSRC
);

  wire and_2_out, not_1_out, not_2_out, not_3_out, not_4_out, not_5_out;

  not not_1 (not_1_out, I14);
  not not_2 (not_2_out, I13);
  not not_3 (not_3_out, I12);
  not not_4 (not_4_out, I5);
  not not_5 (not_5_out, I4);
  and and_1 (ALUCTRL2, I30, not_2_out, I5);
  or or_1 (ALUCTRL1, not_2_out, not_5_out);
  and and_2 (and_2_out, I13, not_3_out);
  or or_2 (ALUSRC, not_4_out, not_5_out);
  or or_3 (ALUCTRL0, not_1_out, and_2_out);

  assign ALUCTRL3 = 1'b0;
endmodule

module DATAPATH (
  input  [31:0] Instruction
);

  wire alucontrol_1_alusrc, clock_1_out;
  wire [3:0] alucontrol_1_aluctrl0;
  wire [31:0] alu32_1_r, bit_extender_1_out, multiplexer_1_out, registerfile_1_rdata1, registerfile_1_rdata2;

  Clock clock_1 (.out(clock_1_out));
  assign bit_extender_1_out = {{20{Instruction[31]}}, Instruction[31:20]};  // Bit_Extender bit_extender_1
  RegisterFile registerfile_1 (
    .RReg2(Instruction[19:15]), .RReg1(Instruction[24:20]), .WData(alu32_1_r), .ClockIn(clock_1_out),
    .Write(1'b1), .WReg(Instruction[11:7]), .RData1(registerfile_1_rdata1), .RData2(registerfile_1_rdata2));
  Multiplexer #(.enable("false"), .width(32)) multiplexer_1 (
    .in0(registerfile_1_rdata2), .in1(bit_extender_1_out), .out(multiplexer_1_out), .sel(alucontrol_1_alusrc));
  ALUControl alucontrol_1 (
    .I30(Instruction[30]), .I14(Instruction[14]), .I13(Instruction[13]), .I12(Instruction[12]),
    .I6(Instruction[6]), .I5(Instruction[5]), .I4(Instruction[4]), .ALUCTRL3(alucontrol_1_aluctrl0[3]),
    .ALUCTRL2(alucontrol_1_aluctrl0[2]), .ALUCTRL1(alucontrol_1_aluctrl0[1]),
    .ALUCTRL0(alucontrol_1_aluctrl0[0]), .ALUSRC(alucontrol_1_alusrc));
  ALU32 alu32_1 (
    .ALU_Ctrl(alucontrol_1_aluctrl0), .A(registerfile_1_rdata1), .B(multiplexer_1_out), .R(alu32_1_r));  // open: Cout
endmodule

module EXTRADataPath (
  input  [31:0] Instruction
);

  wire alucontrlextra_1_alusrc, clock_1_out;
  wire [3:0] alucontrlextra_1_aluctrl0;
  wire [31:0] alu32_1_r, bit_extender_1_out, multiplexer_1_out, registerfile_1_rdata1, registerfile_1_rdata2;

  Clock clock_1 (.out(clock_1_out));
  assign bit_extender_1_out = {{20{Instruction[31]}}, Instruction[31:20]};  // Bit_Extender bit_extender_1
  RegisterFile registerfile_1 (
    .RReg2(Instruction[19:15]), .RReg1(Instruction[24:20]), .WData(alu32_1_r), .ClockIn(clock_1_out),
    .Write(1'b1), .WReg(Instruction[11:7]), .RData1(registerfile_1_rdata1), .RData2(registerfile_1_rdata2));
  Multiplexer #(.enable("false"), .width(32)) multiplexer_1 (
    .in0(registerfile_1_rdata2), .in1(bit_extender_1_out), .out(multiplexer_1_out),
    .sel(alucontrlextra_1_alusrc));
  ALUCONTRLEXTRA alucontrlextra_1 (
    .I30(Instruction[30]), .I14(Instruction[14]), .I13(Instruction[13]), .I12(Instruction[12]),
    .I6(Instruction[6]), .I5(Instruction[5]), .I4(Instruction[4]), .ALUCTRL3(alucontrlextra_1_aluctrl0[3]),
    .ALUCTRL2(alucontrlextra_1_aluctrl0[2]), .ALUCTRL1(alucontrlextra_1_aluctrl0[1]),
    .ALUCTRL0(alucontrlextra_1_aluctrl0[0]), .ALUSRC(alucontrlextra_1_alusrc));
  ALU32 alu32_1 (
    .ALU_Ctrl(alucontrlextra_1_aluctrl0), .A(registerfile_1_rdata1), .B(multiplexer_1_out), .R(alu32_1_r));  // open: Cout
endmodule

module ALUCONTRLEXTRA (
  input  I30,
  input  I14,
  input  I13,
  input  I12,
  input  I6,
  input  I5,
  input  I4,
  output ALUCTRL3,
  output ALUCTRL2,
  output ALUCTRL1,
  output ALUCTRL0,
  output ALUSRC
);

  wire and_3_out, and_4_out, and_5_out, and_6_out, and_7_out, not_1_out, not_2_out, not_3_out, not_4_out,
       not_5_out, not_6_out;

  not not_1 (not_1_out, I30);
  not not_2 (not_2_out, I14);
  not not_3 (not_3_out, I13);
  not not_4 (not_4_out, I12);
  not not_5 (not_5_out, I5);
  not not_6 (not_6_out, I4);
  and and_1 (ALUCTRL3, not_3_out, I12);
  and and_2 (ALUCTRL2, I30, not_3_out, not_4_out, I5);
  and and_3 (and_3_out, not_3_out, not_4_out);
  and and_4 (and_4_out, I30, not_3_out);
  and and_5 (and_5_out, not_2_out, not_4_out);
  and and_6 (and_6_out, I13, not_4_out);
  and and_7 (and_7_out, not_1_out, I14, not_3_out, I12);
  or or_1 (ALUSRC, not_5_out, not_6_out);
  or or_2 (ALUCTRL1, and_3_out, not_6_out, and_4_out);
  or or_3 (ALUCTRL0, and_5_out, and_6_out, and_7_out);
endmodule
